// Digital circuit penasaran_umum_state_machine.dig as structural Verilog
module penasaran_umum_state_machine (
  input  clk
);

  wire multiplexer_1_out, multiplexer_2_out, multiplexer_3_out, multiplexer_4_out, multiplexer_5_out,
       multiplexer_6_out, multiplexer_7_out;
  wire [3:0] d_ff_4_q;
  wire [4:4] maunyebrangkah_out;

  Multiplexer #(.Selector_Bits(5)) multiplexer_1 (
    .sel({maunyebrangkah_out[4], d_ff_4_q}), .in_0(1'b0), .in_1(1'b0), .in_2(1'b0), .in_3(1'b0), .in_4(1'b0),
    .in_5(1'b0), .in_6(1'b0), .in_7(1'b0), .in_8(1'b0), .in_9(1'b1), .in_10(1'b1), .in_11(1'b0),
    .in_12(1'b0), .in_13(1'b0), .in_14(1'b0), .in_15(1'b0), .in_16(1'b1), .in_17(1'b0), .in_18(1'b0),
    .in_19(1'b0), .in_20(1'b0), .in_21(1'b0), .in_22(1'b0), .in_23(1'b0), .in_24(1'b0), .in_25(1'b1),
    .in_26(1'b1), .in_27(1'b0), .in_28(1'b0), .in_29(1'b0), .in_30(1'b0), .in_31(1'b0),
    .out(multiplexer_1_out));
  // Probe on {maunyebrangkah_out[4], d_ff_4_q}
  D_FF d_ff_1 (.D(multiplexer_1_out), .C(clk), .Q(d_ff_4_q[3]));  // open: nQ
  Multiplexer #(.Selector_Bits(5)) multiplexer_2 (
    .sel({maunyebrangkah_out[4], d_ff_4_q}), .in_0(1'b0), .in_1(1'b0), .in_2(1'b0), .in_3(1'b0), .in_4(1'b0),
    .in_5(1'b1), .in_6(1'b1), .in_7(1'b1), .in_8(1'b1), .in_9(1'b0), .in_10(1'b0), .in_11(1'b0),
    .in_12(1'b0), .in_13(1'b0), .in_14(1'b0), .in_15(1'b0), .in_16(1'b0), .in_17(1'b0), .in_18(1'b0),
    .in_19(1'b0), .in_20(1'b0), .in_21(1'b1), .in_22(1'b1), .in_23(1'b1), .in_24(1'b1), .in_25(1'b0),
    .in_26(1'b0), .in_27(1'b0), .in_28(1'b0), .in_29(1'b0), .in_30(1'b0), .in_31(1'b0),
    .out(multiplexer_2_out));
  // Probe on {maunyebrangkah_out[4], d_ff_4_q}
  D_FF d_ff_2 (.D(multiplexer_2_out), .C(clk), .Q(d_ff_4_q[2]));  // open: nQ
  Multiplexer #(.Selector_Bits(5)) multiplexer_3 (
    .sel({maunyebrangkah_out[4], d_ff_4_q}), .in_0(1'b0), .in_1(1'b0), .in_2(1'b0), .in_3(1'b1), .in_4(1'b1),
    .in_5(1'b0), .in_6(1'b0), .in_7(1'b1), .in_8(1'b1), .in_9(1'b0), .in_10(1'b0), .in_11(1'b0),
    .in_12(1'b0), .in_13(1'b0), .in_14(1'b0), .in_15(1'b0), .in_16(1'b1), .in_17(1'b0), .in_18(1'b0),
    .in_19(1'b1), .in_20(1'b1), .in_21(1'b0), .in_22(1'b0), .in_23(1'b1), .in_24(1'b1), .in_25(1'b0),
    .in_26(1'b0), .in_27(1'b0), .in_28(1'b0), .in_29(1'b0), .in_30(1'b0), .in_31(1'b0),
    .out(multiplexer_3_out));
  // Probe on {maunyebrangkah_out[4], d_ff_4_q}
  D_FF d_ff_3 (.D(multiplexer_3_out), .C(clk), .Q(d_ff_4_q[1]));  // open: nQ
  Multiplexer #(.Selector_Bits(5)) multiplexer_4 (
    .sel({maunyebrangkah_out[4], d_ff_4_q}), .in_0(1'b0), .in_1(1'b0), .in_2(1'b1), .in_3(1'b0), .in_4(1'b1),
    .in_5(1'b0), .in_6(1'b1), .in_7(1'b0), .in_8(1'b1), .in_9(1'b0), .in_10(1'b1), .in_11(1'b0),
    .in_12(1'b0), .in_13(1'b0), .in_14(1'b0), .in_15(1'b0), .in_16(1'b0), .in_17(1'b0), .in_18(1'b1),
    .in_19(1'b0), .in_20(1'b1), .in_21(1'b0), .in_22(1'b1), .in_23(1'b0), .in_24(1'b1), .in_25(1'b0),
    .in_26(1'b1), .in_27(1'b0), .in_28(1'b0), .in_29(1'b0), .in_30(1'b0), .in_31(1'b0),
    .out(multiplexer_4_out));
  // Probe on {maunyebrangkah_out[4], d_ff_4_q}
  D_FF d_ff_4 (.D(multiplexer_4_out), .C(clk), .Q(d_ff_4_q[0]));  // open: nQ
  Multiplexer #(.Selector_Bits(4)) multiplexer_5 (
    .sel(d_ff_4_q), .in_0(1'b0), .in_1(1'b0), .in_2(1'b1), .in_3(1'b1), .in_4(1'b1), .in_5(1'b1),
    .in_6(1'b1), .in_7(1'b1), .in_8(1'b1), .in_9(1'b1), .in_10(1'b0), .in_11(1'b0), .in_12(1'b0),
    .in_13(1'b0), .in_14(1'b0), .in_15(1'b0), .out(multiplexer_5_out));
  Multiplexer #(.Selector_Bits(4)) multiplexer_6 (
    .sel(d_ff_4_q), .in_0(1'b0), .in_1(1'b1), .in_2(1'b0), .in_3(1'b0), .in_4(1'b0), .in_5(1'b0),
    .in_6(1'b0), .in_7(1'b0), .in_8(1'b0), .in_9(1'b1), .in_10(1'b1), .in_11(1'b0), .in_12(1'b0),
    .in_13(1'b0), .in_14(1'b0), .in_15(1'b0), .out(multiplexer_6_out));
  Multiplexer #(.Selector_Bits(4)) multiplexer_7 (
    .sel(d_ff_4_q), .in_0(1'b1), .in_1(1'b0), .in_2(1'b0), .in_3(1'b0), .in_4(1'b0), .in_5(1'b0),
    .in_6(1'b0), .in_7(1'b0), .in_8(1'b0), .in_9(1'b0), .in_10(1'b0), .in_11(1'b0), .in_12(1'b0),
    .in_13(1'b0), .in_14(1'b0), .in_15(1'b0), .out(multiplexer_7_out));
  LED led_1 (.in(maunyebrangkah_out[4]));
  LED led_2 (.in(multiplexer_5_out));
  LED led_3 (.in(multiplexer_6_out));
  LED led_4 (.in(multiplexer_7_out));
  // Probe on maunyebrangkah_out[4]
  Button maunyebrangkah (.out(maunyebrangkah_out[4]));
  Seven_Seg_Hex seven_seg_hex_1 (.d(d_ff_4_q), .dp(1'b0));
  LED led_5 ();  // open: in
  LED led_6 ();  // open: in
  LED led_7 ();  // open: in
  LED led_8 ();  // open: in
  LED led_9 ();  // open: in
  LED led_10 ();  // open: in
  LED led_11 ();  // open: in
  LED led_12 ();  // open: in
  LED led_13 ();  // open: in
  LED led_14 ();  // open: in
  LED led_15 ();  // open: in
  LED led_16 ();  // open: in
  LED led_17 ();  // open: in
  LED led_18 ();  // open: in
  LED led_19 ();  // open: in
  LED led_20 ();  // open: in
  LED led_21 ();  // open: in
  LED led_22 ();  // open: in
  LED led_23 ();  // open: in
  LED led_24 ();  // open: in
  LED led_25 ();  // open: in
  LED led_26 ();  // open: in
  LED led_27 ();  // open: in
  LED led_28 ();  // open: in
  LED led_29 ();  // open: in
  LED led_30 ();  // open: in
  LED led_31 ();  // open: in
  LED led_32 ();  // open: in
  LED led_33 ();  // open: in
  LED led_34 ();  // open: in
  LED led_35 ();  // open: in
  LED led_36 ();  // open: in
  LED led_37 ();  // open: in
  LED led_38 ();  // open: in
  LED led_39 ();  // open: in
  LED led_40 ();  // open: in

  // Notes on the sheet:
  //   supaya ketrigger countdown
  //   klo button dipencet
  //   supaya standby di 0
  //   aslinya dont care krn kondisi ini
  //   harusnya ga pernah terjadi 
  //   awaowkoawkoa
  //   supaya bisa count down 
  //   ga terganggu
  //   supaya bisa count down 
  //   ga terganggu juga
  //   JIKA
  //   sekarang...
  //   upkah
  //   0
  //   1
  //   2
  //   3
  //   4
  //   5
  //   6
  //   7
  //   8
  //   9
  //   10
  //   11
  //   12
  //   13
  //   14
  //   15
  //   bit3 bit2 bit1 bit0
  //   0 0 0 0
  //   0 0 0 1
  //   0 0 1 0
  //   0 0 1 1
  //   0 1 0 0
  //   0 1 0 1
  //   0 1 1 0
  //   0 1 1 1
  //   1 0 0 0
  //   1 0 0 1
  //   1 0 1 0
  //   1 0 1 1
  //   1 1 0 0
  //   1 1 0 1
  //   1 1 1 0
  //   1 1 1 1
  //   KLO MAU 
  //   BISA...
  //   DIINGINKAN 
  //   ntar...
  //   NO CHANGE
  //   RESET
  //   PAKE FUNGSI
  //    JKFF YG...
  //   SET
  //   BERARTI KAN DIINGINKAN 
  //   fungsi per  jkffnya...
  //   bit3
  //   MAU PAKE FUNGSI JKFF YG MANA?
  //   TOGGLE
  //   bit2
  //   CARANYA ADALAH
  //   NYETTING JKFF JADI...
  //   bit1
  //   atau
  //   bit0
  //   KLO DIRANGKUM...
  //   MAKA
  //   cara mrogram jkffnya adalah....
  //   x
  //   di JKFF yg ngurusin
  //   dan
  //   berubahnya ...
  //   MAKA 
  //   BUATLAH...
  //   J_3
  //   K_3
  //   CARANYA ADALAH
  //   NYETTING...
  //   HOW CAN I QUINE-MCCLUSKEY EACH OF THESE COLLUMNS TO GET EFFICIENT CIRCUITS??
  //   dan bit2
  //   berubahnya ...
  //   J_2
  //   K_2
  //   dan bit1
  //   berubahnya ...
  //   J_1
  //   K_1
  //   - perlu dikerjakan mandiri,
  //   (karena mau ngukur 
  //   seberapa fasih kalian 
  //   kalau sendirian )
  //   sebagai anak teknik, 
  //   kamu mendapat kepercayaan untuk membuat:
  //   LAMPU PENYEBRANGAN JALAN
  //   30
  //   diharapkan lampumu bisa:
  //   - menyala hijau dalam keadaan standby 
  //   * displaynya 0
  //   ===============
  //   - berhitung mundur ketika tombol
  //    "MENYEBRANGKAH" dipencet
  //   ===============
  //   - berhitung mundur dari A ke 0
  //   (A,9,8,7,6,5,4,3,2,1,0)
  //   tanpa terganggu
  //   ================
  //   - memiliki pola lampu 
  //   saat berhitung mundur 
  //   sebagai berikut:
  //   (silakan ubah desain, 
  //   yg penting masuk akal)
  //   A= kuning
  //   9= kuning & merah
  //   8= merah 
  //   7= merah
  //   6 = merah
  //   5 = merah
  //   4 = merah
  //   3 = merah
  //   2 = merah
  //   1 = kuning
  //   0 = hijau
  //   =============
endmodule
